# Fritzing sketch bom sensor 2 fritzing (saved by Fritzing 0.9.3b)
breadboards: 1

parts:
  Part1 = Arduino Uno (Rev3) - ICSP
  Part2 = 3.5in TFT 480x320 Touch + MicroSD
  MPX1 = MPX2010 pressure sensor [part_number=SSC]
  ZS-042_RTC1 = ZS-042 RTC Module  # not connected

nets:
  N1: Part1.A4/SDA, MPX1.V_out_-
  N2: Part1.A5/SCL, MPX1.GND
  N3: Part1.D8, Part2.LCD_RST_5V
  N4: Part1.D9_PWM, Part2.LCD_RS_5V
  N5: Part1.D10_PWM/SS, Part2.LCD_CS_5V
  N6: Part1.D11_PWM/MOSI, Part2.MOSI
  N7: Part1.D12/MISO, Part2.MISO
  N8: Part1.D13/SCK, Part2.LCD_WR_5V
  5V: Part1.5V, Part2.+5V, MPX1.Vs
  GND: Part1.GND, Part2.GND, MPX1.V_out_+

notes:
  SHT85
  SSCSRNN

custom parts:
  3.5in TFT 480x320 Touch + MicroSD: This TFT display is big (3.5" diagonal), bright (6 white-LED backlight) and colorful! 480x320 pixels with individual RGB pixel control. This display also has a resistive touchscreen attached to it already, so you can detect finger presses anywhere on the screen. There is a controller built into the display with RAM buffering, so that almost no work is done by the microcontroller. The display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
